// Logisim project par3_Data_path_Circuit (1).circ as structural Verilog: 6 circuits, main circuit main
module main (
  input  CLK,
  input  in_2,
  output [15:0] AR,
  output [15:0] DR,
  output [15:0] PC,
  output [15:0] Data_out,
  output [15:0] AC,
  output [15:0] IR,
  output COUT,
  output [11:0] Memory,
  output [2:0] out_11,
  output Read,
  output Write
);

  wire AC_ld, and_1_out, and_2_out, and_3_out, and_4_out, and_5_out, and_6_out, and_7_out, and_8_out,
       and_12_out, and_13_out, and_25_out, and_26_out, and_27_out, and_28_out, and_40_out, and_41_out,
       and_42_out, and_44_out, AR_inr, AR_ld, CIL, CIR, CLA, CLE, CMA, CME, D0, D0T4, D0T5, D1, D1T4, D1T5,
       D2, D2T4, D2T5, D3, D3T4, D4, D4T4, D5, D5T5, D6, D6T4, D6T5, D6T6, D7, D7T3, dpu_1_p1, dpu_1_p3,
       DR_ld, E, e0, Ebar, HLT, INC, indirect, IR_ld, MEM, not_1_out, not_2_out, or_2_out, or_3_out,
       or_4_out, or_5_out, or_6_out, or_10_out, or_13_out, PC_inr, PC_ld, r, S, SNA, SPA, SZA, SZE, T0, T1,
       T2, T3, T4, T5, T6, T7;
  wire [2:0] ALUsel, sel;

  and and_1 (and_1_out, D7T3, CLE);
  and and_2 (and_2_out, D7T3, CME);
  and and_3 (and_3_out, D7T3, CIR);
  or or_1 (Read, D0T4, D1T4, T1, D2T4, D6T4);
  or or_2 (or_2_out, D0T5, D1T5, D2T5, D3T4, D4T4, D5T5, D6T6);
  and and_4 (and_4_out, and_1_out, 1'b0);
  and and_5 (and_5_out, and_2_out, Ebar);
  and and_6 (and_6_out, and_3_out, AC[0]);
  and and_7 (and_7_out, D1T5, COUT);
  and and_8 (and_8_out, D7T3, CIL);
  and and_9 (D0T4, D0, T4);
  and and_10 (D0T5, D0, T5);
  and and_11 (D4T4, D4, T4);
  Decoder #(.select(3)) decoder_1 (
    .out0(D0), .out1(D1), .out2(D2), .out3(D3), .out4(D4), .out5(D5), .out6(D6), .out7(D7), .sel(IR[14:12]));  // open: en
  Counter #(.max('h7), .width(3)) counter_1 (
    .load(or_2_out), .up(1'b1), .count(1'b1), .clk(CLK), .Q(out_11));  // open: clr, D, carry
  and and_12 (and_12_out, and_8_out, AC[15]);
  // dpu dpu_1: pin names not known; wires that end beside it: dpu_1_p1, dpu_1_p1, dpu_1_p3, Write, Read, AR_inr, AR_inr, AR_ld, PC_inr, PC_ld, D6T5, DR_ld, CLA, INC, sel, AC_ld, E, E, ALUsel, IR_ld, Data_out, CLK, AR, PC, DR, AC, IR, Memory, COUT
  D_Flip_Flop d_ff_1 (.D(or_3_out), .clk(CLK), .Q(E), .Qn(Ebar));  // open: preset, reset
  or or_3 (or_3_out, and_7_out, and_4_out, and_5_out, and_6_out, and_12_out);
  and and_13 (and_13_out, D7T3, HLT);
  D_Flip_Flop d_ff_2 (.D(and_13_out), .clk(CLK), .Q(S));  // open: Qn, preset, reset
  and and_14 (D1T4, D1, T4);
  and and_15 (D1T5, D1, T5);
  and and_16 (AR_inr, D5, T4);
  and and_17 (D5T5, D5, T5);
  Decoder #(.select(3)) decoder_2 (
    .out0(T0), .out1(T1), .out2(T2), .out3(T3), .out4(T4), .out5(T5), .out6(T6), .out7(T7), .sel(out_11));  // open: en
  and and_18 (D2T4, D2, T4);
  and and_19 (D2T5, D2, T5);
  and and_20 (D6T4, D6, T4);
  and and_21 (D6T5, D6, T5);
  and and_22 (D6T6, D6, T6);
  RAM #(.addrWidth(12), .dataWidth(16)) ram_1 (
    .addr(Memory), .we(Write), .oe(Read), .clk(CLK), .din(AR), .dout(Data_out));
  and and_23 (D3T4, D3, T4);
  and and_24 (D7T3, D7, T3);
  or or_4 (or_4_out, D0T4, D1T4, D2T4, D6T4);
  or or_5 (or_5_out, T0, T1);
  or or_6 (or_6_out, T1, T2);
  or or_7 (sel[2], or_6_out, D3T4, or_4_out);
  // Probe on sel
  and and_25 (and_25_out, e0, SZE);
  and and_26 (and_26_out, AC[0], SZA);
  not not_1 (not_1_out, AC[15]);
  and and_27 (and_27_out, not_1_out, SPA);
  and and_28 (and_28_out, AC[15], SNA);
  buf or_8 (IR_ld, T1);  // OR_Gate
  or or_9 (AR_ld, T0, T2, indirect);
  or or_10 (or_10_out, D7, T3, CMA);
  or or_11 (sel[1], or_4_out, AR_inr, D6T6, or_5_out);
  or or_12 (sel[0], or_6_out, D4T4, D6T6, D5T5, or_4_out);
  and and_29 (and_28_out, T6, D6);
  not not_2 (not_2_out, IR[15]);
  or or_13 (or_13_out, D7, T3, CIR);
  and and_30 (indirect, T3, MEM, IR[15]);
  and and_31 (r, not_2_out, D7);
  or or_14 (PC_inr, and_25_out, and_26_out, and_27_out, and_28_out, and_28_out, T1);
  or or_15 (DR_ld, D0T4, D1T4, D2T4, D6T4);
  or or_16 (AC_ld, D0T5, D1T5, or_13_out, D2T5, or_10_out);
  or or_17 (Write, D3T4, D6T6, AR_inr);
  or or_18 (PC_ld, D4T4, D5T5);
  or or_19 (ALUsel[1], CMA, CIL, D1T5);
  or or_20 (ALUsel[2], D2T5, CIL, CIR);
  // Probe on ALUsel
  or or_21 (ALUsel[0], CMA, CIR, D0T5);
  Comparator #(.width(1)) comparator_1 (.a(E), .b(in_2), .eq(e0));  // open: gt, lt
  and and_32 (CLA, r, IR[11]);
  and and_33 (CLE, r, IR[10]);
  or or_22 (MEM, D0, D1, D2, D3, D4, D5, D6, D7);
  and and_34 (CMA, r, IR[9]);
  and and_35 (CME, r, IR[8]);
  and and_36 (CIR, r, IR[7]);
  and and_37 (CIL, r, IR[6]);
  and and_38 (INC, r, IR[5]);
  and and_39 (SPA, T3, and_40_out);
  and and_40 (and_40_out, r, IR[4]);
  and and_41 (and_41_out, r, IR[3]);
  and and_42 (and_42_out, r, IR[2]);
  and and_43 (SNA, T3, and_41_out);
  and and_44 (and_44_out, r, IR[1]);
  and and_45 (HLT, r, IR[0]);
  and and_46 (SZA, T3, and_42_out);
  and and_47 (SZE, T3, and_44_out);

  // Other names for the same wires on the sheet: ac0_t = AC[0]; AC_out[15:0] = AC; C_out = COUT; D5T4 = AR_inr;
  //   Data_in[15:0] = Data_out; DR_inr = D6T5; DR_out[15:0] = DR; address[11:0] = IR[11:0]; D[2:0] = IR[14:12];
  //   I = IR[15]
endmodule

module ALU (
  input  [15:0] DR,
  input  [15:0] AC,
  input  [7:0] INPR,
  input  I_L,
  input  I_R,
  input  [2:0] S2S1S0,
  output [15:0] Data_out,
  output Cout
);

  wire [15:0] adder_1_out, and_1_out, not_1_out;

  assign and_1_out = DR & AC;  // AND_Gate and_1, 16 bits wide
  Adder #(.width(16)) adder_1 (.a(DR), .b(AC), .out(adder_1_out), .cout(Cout));  // open: cin
  assign not_1_out = ~AC;  // NOT_Gate not_1, 16 bits wide
  Multiplexer #(.select(3), .width(16)) multiplexer_1 (
    .in0(AC), .in1(and_1_out), .in2(adder_1_out), .in3(not_1_out), .in4(DR), .in5({I_R, AC[15:1]}),
    .in6({AC[14:0], I_L}), .in7({{8{1'b0}}, INPR}), .out(Data_out), .sel(S2S1S0));
endmodule

module dpu (
  input  write,
  input  read,
  input  AR_clr,
  input  AR_inr,
  input  AR_ld,
  input  PC_clr,
  input  PC_inr,
  input  PC_ld,
  input  DR_clr,
  input  DR_inr,
  input  DR_ld,
  input  AC_clr,
  input  AC_inr,
  input  [2:0] sel,
  input  AC_ld,
  input  [7:0] INPR,
  input  i_l,
  input  i_r,
  input  [2:0] ALUsel,
  input  IR_ld,
  input  TR_clr,
  input  TR_inr,
  input  TR_ld,
  input  [15:0] data_in,
  input  clk,
  output [15:0] AR_out,
  output [15:0] PC_out,
  output [15:0] DR_out,
  output [15:0] AC_out,
  output [15:0] IR_out,
  output [15:0] DATA_OUT,
  output [11:0] MEMORY,
  output Cout
);

  wire [15:0] alu_1_data_out, ram_1_dout, register16bit_4_dataout;

  ALU alu_1 (
    .DR(DR_out), .AC(AC_out), .INPR(INPR), .I_L(i_l), .I_R(i_r), .S2S1S0(ALUsel), .Data_out(alu_1_data_out),
    .Cout(Cout));
  // Probe on MEMORY
  register12bit register12bit_1 (
    .CLR(AR_clr), .INR(AR_inr), .LD(AR_ld), .CLK(clk), .DataIn(data_in), .DataOut(AR_out), .Memory(MEMORY));
  register16bit register16bit_1 (.CLR(PC_clr), .INR(PC_inr), .DataIn(data_in), .LD(PC_ld), .CLK(clk), .DataOut(PC_out));
  register16bit register16bit_2 (.CLR(DR_clr), .INR(DR_inr), .DataIn(data_in), .LD(DR_ld), .CLK(clk), .DataOut(DR_out));
  register16bit register16bit_3 (
    .CLR(AC_clr), .INR(AC_inr), .DataIn(alu_1_data_out), .LD(AC_ld), .CLK(clk), .DataOut(AC_out));
  InformationRegister informationregister_1 (.DataIn(data_in), .LD(IR_ld), .DataOut(IR_out));
  register16bit register16bit_4 (
    .CLR(TR_clr), .INR(TR_inr), .DataIn(data_in), .LD(TR_ld), .CLK(clk), .DataOut(register16bit_4_dataout));
  RAM #(.addrWidth(12), .dataWidth(16)) ram_1 (
    .addr(MEMORY), .we(write), .oe(read), .clk(clk), .din(data_in), .dout(ram_1_dout));
  // Probe on AC_out
  // Probe on PC_out
  // Probe on IR_out
  // Probe on register16bit_4_dataout
  // Probe on DR_out
  // Probe on AR_out
  // Probe on ram_1_dout
  Multiplexer #(.select(3), .width(16)) multiplexer_1 (
    .in1(AR_out), .in2(PC_out), .in3(DR_out), .in4(AC_out), .in5(IR_out), .in6(register16bit_4_dataout),
    .in7(ram_1_dout), .out(DATA_OUT), .sel(sel));  // open: in0
  // Probe on DATA_OUT

  // Other names for the same wires on the sheet: DATA_IN_t[15:0] = DATA_OUT
endmodule

module register16bit (
  input  CLR,
  input  INR,
  input  [15:0] DataIn,
  input  LD,
  input  CLK,
  output [15:0] DataOut
);

  wire [15:0] adder_1_out, multiplexer_1_out, multiplexer_2_out, multiplexer_3_out;

  Multiplexer #(.width(16)) multiplexer_1 (.in0(DataOut), .in1({16{1'b0}}), .out(multiplexer_1_out), .sel(CLR));
  Adder #(.width(16)) adder_1 (.a(16'h1), .b(DataOut), .out(adder_1_out));  // open: cin, cout
  Multiplexer #(.width(16)) multiplexer_2 (
    .in0(multiplexer_1_out), .in1(adder_1_out), .out(multiplexer_2_out), .sel(INR));
  Multiplexer #(.width(16)) multiplexer_3 (.in0(multiplexer_2_out), .in1(DataIn), .out(multiplexer_3_out), .sel(LD));
  Register #(.width(16)) register_1 (.D(multiplexer_3_out), .clk(CLK), .Q(DataOut));  // open: en, clr
endmodule

module InformationRegister (
  input  [15:0] DataIn,
  input  LD,
  output [15:0] DataOut
);

  wire clock_1_out;
  wire [15:0] multiplexer_1_out;

  Multiplexer #(.width(16)) multiplexer_1 (.in0(DataOut), .in1(DataIn), .out(multiplexer_1_out), .sel(LD));
  Clock clock_1 (.out(clock_1_out));
  Register #(.width(16)) register_1 (.D(multiplexer_1_out), .clk(clock_1_out), .Q(DataOut));  // open: en, clr
endmodule

module register12bit (
  input  CLR,
  input  INR,
  input  LD,
  input  CLK,
  input  [15:0] DataIn,
  output [15:0] DataOut,
  output [11:0] Memory
);

  wire [11:0] adder_1_out, multiplexer_1_out, multiplexer_2_out, multiplexer_3_out;

  Multiplexer #(.width(12)) multiplexer_1 (.in0(DataOut[11:0]), .in1({12{1'b0}}), .out(multiplexer_1_out), .sel(CLR));
  Adder #(.width(12)) adder_1 (.a(12'h1), .b(DataOut[11:0]), .out(adder_1_out));  // open: cin, cout
  Multiplexer #(.width(12)) multiplexer_2 (
    .in0(multiplexer_1_out), .in1(adder_1_out), .out(multiplexer_2_out), .sel(INR));
  Multiplexer #(.width(12)) multiplexer_3 (
    .in0(multiplexer_2_out), .in1(DataIn[11:0]), .out(multiplexer_3_out), .sel(LD));
  Register #(.width(12)) register_1 (.D(multiplexer_3_out), .clk(CLK), .Q(DataOut[11:0]));  // open: en, clr

  assign DataOut[15:12] = 4'b0000;
  assign Memory = DataOut[11:0];
endmodule
