// Logisim project par3_Data_path_Circuit.circ as structural Verilog: 10 circuits, main circuit main
module main (
  output [2:0] out_1
);

  wire D0, D0T4, D0T5, D1, D1T4, D1T5, D2, D3, D4, D5, D6, D7, I, indirect, not_1_out, or_1_out, or_2_out,
       or_3_out, or_4_out, T0, T1, T2, T3, T4, T5, T6, T7;
  wire [2:0] D;
  wire [2:1] sel;
  wire [11:0] data_path_unit_1_ir_out;

  buf or_1 (or_1_out, D0T5);  // OR_Gate
  and and_1 (D0T4, D0, T4);
  and and_2 (D0T5, D0, T5);
  Decoder #(.select(3)) decoder_1 (
    .out0(D0), .out1(D1), .out2(D2), .out3(D3), .out4(D4), .out5(D5), .out6(D6), .out7(D7), .sel(D));  // open: en
  Counter #(.max('h7), .width(3)) counter_1 (.clr(or_1_out), .Q(out_1));  // open: load, up, count, clk, D, carry
  and and_3 (D1T4, D1, T4);
  and and_4 (D1T5, D1, T5);
  or or_2 (or_2_out, T0, T2, indirect);
  or or_3 (or_3_out, D0T4, D1T4);
  buf or_4 (or_4_out, D0T5);  // OR_Gate
  Decoder #(.select(3)) decoder_2 (
    .out0(T0), .out1(T1), .out2(T2), .out3(T3), .out4(T4), .out5(T5), .out6(T6), .out7(T7), .sel(out_1));  // open: en
  data_path_unit data_path_unit_1 (
    .read(T1), .AR_ld(or_2_out), .PC_inr(T1), .sel({sel, sel[2]}), .DR_ld(or_3_out), .IR_ld(T1),
    .AC_LD(or_4_out), .IR_OUT({I, D, data_path_unit_1_ir_out}));  // open: write, AR_clr, AR_inr, PC_clr, pc_ld, DR_clr, DR_inr, AC_CLR, Shift_right, Shift_left, inpr, AC_INR, TR_clr, TR_inr, TR_ld, COUT
  or or_5 (sel[1], T0, T1);
  or or_6 (sel[2], T1, T2);
  not not_1 (not_1_out, D7);
  and and_5 (indirect, T3, not_1_out, I);

  // Other names for the same wires on the sheet: sel[0] = sel[2]
endmodule

module Data_Register (
  input  CLR,
  input  CLK,
  input  INR,
  input  [15:0] DR_input,
  input  LD,
  output [15:0] DR_output
);

  wire [15:0] adder_1_out, multiplexer_1_out, multiplexer_2_out, multiplexer_3_out;

  Multiplexer #(.width(16)) multiplexer_1 (.in0(DR_output), .in1({16{1'b0}}), .out(multiplexer_1_out), .sel(CLR));
  Adder #(.width(16)) adder_1 (.a(16'h1), .b(DR_output), .out(adder_1_out));  // open: cin, cout
  Multiplexer #(.width(16)) multiplexer_2 (
    .in0(multiplexer_1_out), .in1(adder_1_out), .out(multiplexer_2_out), .sel(INR));
  Multiplexer #(.width(16)) multiplexer_3 (.in0(multiplexer_2_out), .in1(DR_input), .out(multiplexer_3_out), .sel(LD));
  Register #(.width(16)) register_1 (.D(multiplexer_3_out), .clk(CLK), .Q(DR_output));  // open: en, clr

  // Notes on the sheet:
  //   Data Register
endmodule

module Address_register (
  input  CLR,
  input  CLK,
  input  INR,
  input  LD,
  input  [15:0] AR_input,
  output [11:0] Memory,
  output [15:0] AR_Output
);

  wire [11:0] adder_1_out, multiplexer_1_out, multiplexer_2_out, multiplexer_3_out;

  Multiplexer #(.width(12)) multiplexer_1 (.in0(AR_Output[11:0]), .in1({12{1'b0}}), .out(multiplexer_1_out), .sel(CLR));
  Adder #(.width(12)) adder_1 (.a(12'h1), .b(AR_Output[11:0]), .out(adder_1_out));  // open: cin, cout
  Multiplexer #(.width(12)) multiplexer_2 (
    .in0(multiplexer_1_out), .in1(adder_1_out), .out(multiplexer_2_out), .sel(INR));
  Multiplexer #(.width(12)) multiplexer_3 (
    .in0(multiplexer_2_out), .in1(AR_input[11:0]), .out(multiplexer_3_out), .sel(LD));
  Register #(.width(12)) register_1 (.D(multiplexer_3_out), .clk(CLK), .Q(AR_Output[11:0]));  // open: en, clr

  assign AR_Output[15:12] = 4'b0000;
  assign Memory = AR_Output[11:0];

  // Notes on the sheet:
  //   Address Register
endmodule

module Program_counter (
  input  CLR,
  input  CLK,
  input  INR,
  input  [15:0] PC_input,
  input  LD,
  output [15:0] PC_output
);

  wire [15:0] adder_1_out, multiplexer_1_out, multiplexer_2_out, multiplexer_3_out;

  Multiplexer #(.width(16)) multiplexer_1 (.in0(PC_output), .in1({16{1'b0}}), .out(multiplexer_1_out), .sel(CLR));
  Adder #(.width(16)) adder_1 (.a(16'h1), .b(PC_output), .out(adder_1_out));  // open: cin, cout
  Multiplexer #(.width(16)) multiplexer_2 (
    .in0(multiplexer_1_out), .in1(adder_1_out), .out(multiplexer_2_out), .sel(INR));
  Multiplexer #(.width(16)) multiplexer_3 (.in0(multiplexer_2_out), .in1(PC_input), .out(multiplexer_3_out), .sel(LD));
  Register #(.width(16)) register_1 (.D(multiplexer_3_out), .clk(CLK), .Q(PC_output));  // open: en, clr

  // Notes on the sheet:
  //   Program_Counter
endmodule

module Instruction_Register (
  input  CLK,
  input  [15:0] IR_input,
  input  LD,
  output [15:0] IR_output
);

  wire [15:0] multiplexer_1_out;

  Multiplexer #(.width(16)) multiplexer_1 (.in0(IR_output), .in1(IR_input), .out(multiplexer_1_out), .sel(LD));
  Register #(.width(16)) register_1 (.D(multiplexer_1_out), .clk(CLK), .Q(IR_output));  // open: en, clr
endmodule

module Temp_Register (
  input  CLR,
  input  CLK,
  input  [15:0] TEMP_input,
  input  INR,
  input  LD,
  output [15:0] TEMP_output
);

  wire [15:0] adder_1_out, multiplexer_1_out, multiplexer_2_out, multiplexer_3_out;

  Multiplexer #(.width(16)) multiplexer_1 (.in0(TEMP_output), .in1({16{1'b0}}), .out(multiplexer_1_out), .sel(CLR));
  Adder #(.width(16)) adder_1 (.a(16'h1), .b(TEMP_output), .out(adder_1_out));  // open: cin, cout
  Multiplexer #(.width(16)) multiplexer_2 (
    .in0(multiplexer_1_out), .in1(adder_1_out), .out(multiplexer_2_out), .sel(INR));
  Multiplexer #(.width(16)) multiplexer_3 (
    .in0(multiplexer_2_out), .in1(TEMP_input), .out(multiplexer_3_out), .sel(LD));
  Register #(.width(16)) register_1 (.D(multiplexer_3_out), .clk(CLK), .Q(TEMP_output));  // open: en, clr

  // Notes on the sheet:
  //   Temp Register
endmodule

module ALU (
  input  [15:0] NOP,
  input  [15:0] A,
  input  [15:0] B,
  input  R,
  input  L,
  input  [7:0] INPR,
  input  [2:0] Sel,
  output [15:0] out_put,
  output Cout
);

  wire [15:0] adder_1_out, and_1_out, not_1_out;

  assign and_1_out = A & B;  // AND_Gate and_1, 16 bits wide
  Adder #(.width(16)) adder_1 (.a(A), .b(B), .out(adder_1_out), .cout(Cout));  // open: cin
  assign not_1_out = ~A;  // NOT_Gate not_1, 16 bits wide
  Multiplexer #(.select(3), .width(16)) multiplexer_1 (
    .in0(NOP), .in1(and_1_out), .in2(adder_1_out), .in3(not_1_out), .in4(B), .in5({R, A[15:1]}),
    .in6({A[14:0], L}), .in7({{8{1'b0}}, INPR}), .out(out_put), .sel(Sel));
endmodule

module data_path_unit (
  input  write,
  input  read,
  input  AR_clr,
  input  AR_inr,
  input  AR_ld,
  input  PC_clr,
  input  PC_inr,
  input  [2:0] sel,
  input  pc_ld,
  input  DR_clr,
  input  DR_inr,
  input  DR_ld,
  input  IR_ld,
  input  AC_CLR,
  input  Shift_right,
  input  Shift_left,
  input  [7:0] inpr,
  input  AC_INR,
  input  AC_LD,
  input  TR_clr,
  input  TR_inr,
  input  TR_ld,
  output [15:0] IR_OUT,
  output COUT
);

  wire clk_out;
  wire [11:0] address_register_1_memory;
  wire [15:0] accumulator_1_ac_output, address_register_1_ar_output, alu_1_out_put, DR, multiplexer_1_out,
       program_counter_1_pc_output, ram_1_dout, temp_register_1_temp_output;

  Clock clk (.out(clk_out));
  Address_register address_register_1 (
    .CLR(AR_clr), .CLK(clk_out), .INR(AR_inr), .LD(AR_ld), .AR_input(multiplexer_1_out),
    .Memory(address_register_1_memory), .AR_Output(address_register_1_ar_output));
  Program_counter program_counter_1 (
    .CLR(PC_clr), .CLK(clk_out), .INR(PC_inr), .PC_input(multiplexer_1_out), .LD(pc_ld),
    .PC_output(program_counter_1_pc_output));
  // Probe on program_counter_1_pc_output
  Data_Register data_register_1 (
    .CLR(DR_clr), .CLK(clk_out), .INR(DR_inr), .DR_input(multiplexer_1_out), .LD(DR_ld), .DR_output(DR));
  // Probe on DR
  Instruction_Register instruction_register_1 (
    .CLK(clk_out), .IR_input(multiplexer_1_out), .LD(IR_ld), .IR_output(IR_OUT));
  // Probe on IR_OUT
  ALU alu_1 (
    .NOP(accumulator_1_ac_output), .A(accumulator_1_ac_output), .B(DR), .R(Shift_right), .L(Shift_left),
    .INPR(inpr), .Sel(IR_OUT[14:12]), .out_put(alu_1_out_put), .Cout(COUT));
  Temp_Register temp_register_1 (
    .CLR(TR_clr), .CLK(clk_out), .TEMP_input(multiplexer_1_out), .INR(TR_inr), .LD(TR_ld),
    .TEMP_output(temp_register_1_temp_output));
  // Probe on address_register_1_memory
  // Probe on temp_register_1_temp_output
  // Probe on address_register_1_ar_output
  // Probe on accumulator_1_ac_output
  Accumulator accumulator_1 (
    .CLR(AC_CLR), .CLK(clk_out), .INR(AC_INR), .AC_input(alu_1_out_put), .LD(AC_LD),
    .AC_output(accumulator_1_ac_output));
  Multiplexer #(.select(3), .width(16)) multiplexer_1 (
    .in1(address_register_1_ar_output), .in2(program_counter_1_pc_output), .in3(DR),
    .in4(accumulator_1_ac_output), .in5(IR_OUT), .in6(temp_register_1_temp_output), .in7(ram_1_dout),
    .out(multiplexer_1_out), .sel(sel));  // open: in0
  RAM #(.addrWidth(12), .dataWidth(16)) ram_1 (
    .addr(address_register_1_memory), .we(write), .oe(read), .clk(clk_out), .dout(ram_1_dout));  // open: din
  // Probe on ram_1_dout

  // Other names for the same wires on the sheet: SEL_t[2:0] = IR_OUT[14:12]
endmodule

module Accumulator (
  input  CLR,
  input  CLK,
  input  INR,
  input  [15:0] AC_input,
  input  LD,
  output [15:0] AC_output
);

  wire [15:0] adder_1_out, multiplexer_1_out, multiplexer_2_out, multiplexer_3_out;

  Multiplexer #(.width(16)) multiplexer_1 (.in0(AC_output), .in1({16{1'b0}}), .out(multiplexer_1_out), .sel(CLR));
  Adder #(.width(16)) adder_1 (.a(16'h1), .b(AC_output), .out(adder_1_out));  // open: cin, cout
  Multiplexer #(.width(16)) multiplexer_2 (
    .in0(multiplexer_1_out), .in1(adder_1_out), .out(multiplexer_2_out), .sel(INR));
  Multiplexer #(.width(16)) multiplexer_3 (.in0(multiplexer_2_out), .in1(AC_input), .out(multiplexer_3_out), .sel(LD));
  Register #(.width(16)) register_1 (.D(multiplexer_3_out), .clk(CLK), .Q(AC_output));  // open: en, clr

  // Notes on the sheet:
  //   Accumulator
endmodule

module add (
  input  D0,
  input  T4,
  input  T5
);
endmodule
